# Fritzing sketch btn_gpio (saved by Fritzing 0.9.2b)
breadboards: 1

parts:
  Raspberry_Pi1 = Raspberry Pi 2
  R1 = Resistor [tolerance=±5% resistance=330 package=THT]
  LED1 = LED - 5mm [color="Red (633nm)" package="5 mm [THT]"]
  S1 = Pushbutton [package="[THT]"]

nets (from the schematic view):
  N1: Raspberry_Pi1.3v3, R1.Pin_0
  N2: Raspberry_Pi1.GND, LED1.cathode
  N3: R1.Pin_1, LED1.anode
  N4: S1.Pin_1, S1.Pin_2
  N5: S1.Pin_3, S1.Pin_4
